# Fritzing sketch PCB TRUFES (2) (saved by Fritzing 0.9.3b)
circuit board: 10cm x 10cm
breadboards: 1

parts:
  R1 = Resistor [tolerance=±5% resistance=220 package=THT]
  Bateria = Battery
  ultrassom = Humidity and Temperature Sensor RHT03
  Ultrassom2 = Humidity and Temperature Sensor RHT03
  Nano = Arduino Nano (Rev3.0)
  R10 = Resistor [tolerance=±5% resistance=220 package=THT]
  R11 = Resistor [tolerance=±5% resistance=220 package=THT]
  R14 = Resistor [tolerance=±5% resistance=220 package=THT]
  J1 = female pin header, 2 pins [form="♀ (female)"]
  J2 = female pin header, 2 pins [form="♀ (female)"]
  Motor_1(Esq) = female pin header, 2 pins [form="♀ (female)"]
  Q1 = NPN-Transistor [package="TO92 [THT]"]
  Motor_1(Esq)1 = female pin header, 2 pins [form="♀ (female)"]
  Q2 = NPN-Transistor [package="TO92 [THT]"]
  ultrassom1 = Humidity and Temperature Sensor RHT03
  ultrassom2 = Humidity and Temperature Sensor RHT03
  S2 = Toggle Switch [package=THT]
  J3 = female pin header, 6 pins [form="♀ (female)"]
  R19 = Resistor [tolerance=±5% resistance=220 package=THT]
  R20 = Resistor [tolerance=±5% resistance=220 package=THT]
  J4 = female pin header, 8 pins [form="♀ (female)"]
  R21 = Resistor [tolerance=±5% resistance=220 package=THT]
  R22 = Resistor [tolerance=±5% resistance=220 package=THT]
  J5 = female pin header, 2 pins [form="♀ (female)"]

nets:
  N1: R1.Pin_0, Nano.A7, J2.pin2
  N2: R1.Pin_1, Bateria.-, ultrassom.GND_2, Ultrassom2.GND_2, Nano.GND, R14.Pin_1, Q1.E, Q2.E, ultrassom1.GND_2, ultrassom2.GND_2, J4.pin2, J4.pin4, J4.pin6, J4.pin8, J5.pin2
  N3: Bateria.+, S2.L2, J5.pin1
  VCC: ultrassom.Vcc, Ultrassom2.Vcc, Nano.5V, J1.pin1, J2.pin1, ultrassom1.Vcc, ultrassom2.Vcc
  N4: ultrassom.Data-signal, Ultrassom2.Data-signal, Nano.D5, ultrassom1.Data-signal, ultrassom2.Data-signal
  N5: ultrassom.GND_1, Nano.D4
  N6: Ultrassom2.GND_1, Nano.D9
  N7: Nano.D3, R22.Pin_1
  N8: Nano.D6, J3.pin1, J3.pin6
  N9: Nano.D8, J3.pin2, J3.pin5
  N10: Nano.D10, J3.pin3, J3.pin4
  N11: Nano.D11/MOSI, R21.Pin_1
  N12: Nano.VIN, Motor_1(Esq).pin2, Motor_1(Esq)1.pin2, S2.COM
  N13: Nano.A6, R14.Pin_0, J1.pin2
  N14: Nano.A5, ultrassom1.GND_1
  N15: Nano.A4, ultrassom2.GND_1
  N16: Nano.A3, R10.Pin_0
  N17: Nano.A2, R11.Pin_0
  N18: Nano.A1, R19.Pin_0
  N19: Nano.A0, R20.Pin_0
  N20: R10.Pin_1, J4.pin7
  N21: R11.Pin_1, J4.pin5
  N22: Motor_1(Esq).pin1, Q1.C
  N23: Q1.B, R22.Pin_0
  N24: Motor_1(Esq)1.pin1, Q2.C
  N25: Q2.B, R21.Pin_0
  N26: R19.Pin_1, J4.pin3
  N27: R20.Pin_1, J4.pin1
