# Fritzing sketch PCB TRUFES_NOVO (saved by Fritzing 0.9.3b)
circuit board: 10cm x 10cm
breadboards: 1

parts:
  R1 = Resistor [tolerance=±5% resistance=220 package=THT]
  Bateria = Battery
  ultrassom = Humidity and Temperature Sensor RHT03
  Ultrassom2 = Humidity and Temperature Sensor RHT03
  R10 = Resistor [tolerance=±5% resistance=220 package=THT]
  R11 = Resistor [tolerance=±5% resistance=220 package=THT]
  R14 = Resistor [tolerance=±5% resistance=220 package=THT]
  J1 = female pin header, 2 pins [form="♀ (female)"]
  J2 = female pin header, 2 pins [form="♀ (female)"]
  Motor_1(Esq) = female pin header, 2 pins [form="♀ (female)"]
  Q1 = NPN-Transistor [package="TO92 [THT]"]
  Motor_1(Esq)1 = female pin header, 2 pins [form="♀ (female)"]
  Q2 = NPN-Transistor [package="TO92 [THT]"]
  ultrassom1 = Humidity and Temperature Sensor RHT03
  ultrassom2 = Humidity and Temperature Sensor RHT03
  S2 = Toggle Switch [package=THT]
  J3 = female pin header, 6 pins [form="♀ (female)"]
  R19 = Resistor [tolerance=±5% resistance=220 package=THT]
  R20 = Resistor [tolerance=±5% resistance=220 package=THT]
  J4 = female pin header, 8 pins [form="♀ (female)"]
  R21 = Resistor [tolerance=±5% resistance=220 package=THT]
  R22 = Resistor [tolerance=±5% resistance=220 package=THT]
  J5 = female pin header, 2 pins [form="♀ (female)"]
  Nano = Arduino Nano (Rev3.0)

nets:
  N1: R1.Pin_0, J2.pin2, Nano.A7
  N2: R1.Pin_1, Bateria.-, ultrassom.GND_2, Ultrassom2.GND_2, R14.Pin_1, Q1.E, Q2.E, ultrassom1.GND_2, ultrassom2.GND_2, J4.pin2, J4.pin4, J4.pin6, J4.pin8, J5.pin2, Nano.GND
  N3: Bateria.+, S2.L2, J5.pin1
  VCC: ultrassom.Vcc, Ultrassom2.Vcc, J1.pin1, J2.pin1, ultrassom1.Vcc, ultrassom2.Vcc, Nano.5V
  N4: ultrassom.Data-signal, Ultrassom2.Data-signal, ultrassom1.Data-signal, ultrassom2.Data-signal, Nano.D5
  N5: ultrassom.GND_1, Nano.D4
  N6: Ultrassom2.GND_1, Nano.D8
  N7: R10.Pin_0, Nano.A3
  N8: R10.Pin_1, J4.pin7
  N9: R11.Pin_0, Nano.A2
  N10: R11.Pin_1, J4.pin5
  N11: R14.Pin_0, J1.pin2, Nano.A6
  N12: Motor_1(Esq).pin1, Q1.C
  N13: Motor_1(Esq).pin2, Motor_1(Esq)1.pin2, S2.COM, Nano.VIN
  N14: Q1.B, R22.Pin_0
  N15: Motor_1(Esq)1.pin1, Q2.C
  N16: Q2.B, R21.Pin_0
  N17: ultrassom1.GND_1, Nano.A5
  N18: ultrassom2.GND_1, Nano.A4
  N19: J3.pin1, J3.pin6, Nano.D6
  N20: J3.pin2, J3.pin5, Nano.D9
  N21: J3.pin3, J3.pin4, Nano.D10
  N22: R19.Pin_0, Nano.A1
  N23: R19.Pin_1, J4.pin3
  N24: R20.Pin_0, Nano.A0
  N25: R20.Pin_1, J4.pin1
  N26: R21.Pin_1, Nano.D11/MOSI
  N27: R22.Pin_1, Nano.D3
